# Fritzing sketch pico-and-oled (saved by Fritzing 0.9.4)
breadboards: 1

parts:
  Part1 = OLED Monochrome 128x32 I2C [part_number=931]
  Pico1 = Raspberry Pi Pico

nets:
  VIN: Part1.VIN, Pico1.3V3
  GND: Part1.GND, Pico1.GND
  N1: Part1.SCL, Pico1.GP9
  N2: Part1.SDA, Pico1.GP8

custom parts:
  OLED Monochrome 128x32 I2C: These displays are small, only about 1" diagonal, but very readable due to the high contrast of an OLED display. This display is made of 128x32 individual white OLED pixels, each one is turned on or off by the controller chip. Because the display makes its own light, no backlight is required. This reduces the power required to run the OLED and is why the display has such high contrast; we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
  Raspberry Pi Pico: Raspberry Pi Pico. Based around the RP2040 microcontroller the Pico is a low cost microcontroller device bringing Raspberry Pi quality, cost, and easy of use to the microcontroller space.
