# Fritzing sketch neopixel_ring (saved by Fritzing 0.9.4)
breadboards: 1

parts:
  Pico1 = Raspberry Pi Pico
  Part2 = 16 NeoPixel Ring [part_number=1463]

nets:
  GND: Pico1.GND, Part2.GND
  3V3: Pico1.3V3, Part2.VDD
  N1: Pico1.GP6, Part2.IN

custom parts:
  Raspberry Pi Pico: Raspberry Pi Pico. Based around the RP2040 microcontroller the Pico is a low cost microcontroller device bringing Raspberry Pi quality, cost, and easy of use to the microcontroller space.
  16 NeoPixel Ring: 16 ultra bright smart LED NeoPixels are arranged in a circle with 1.75" (44.5mm) outer diameter. The rings are 'chainable' - connect the output pin of one to the input pin of another. Use only one microcontroller pin to control as many as you can chain together! Each LED is addressable as the driver chip is inside the LED. Each one has ~18mA constant current drive so the color will be very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
